# Fritzing sketch InputModule (saved by Fritzing 1.0.7)
circuit board: 6.10996cm x 4.10542cm
breadboards: 1

parts:
  RE1 = Rotary Encoder [package=THT]
  V1 = DC Power [voltage=3.3V]
  MX2 = Cherry MX Keyswitch Simple
  MX3 = Cherry MX Keyswitch Simple
  MX5 = Cherry MX Keyswitch Simple
  MX4 = Cherry MX Keyswitch Simple
  C11 = Ceramic Capacitor [capacitance=10nF voltage=35V package="1206 [SMD, multilayer]"]
  C9 = Ceramic Capacitor [capacitance=10nF voltage=35V package="1206 [SMD, multilayer]"]
  C10 = Ceramic Capacitor [capacitance=10nF voltage=35V package="1206 [SMD, multilayer]"]
  C12 = Ceramic Capacitor [capacitance=10nF voltage=35V package="1206 [SMD, multilayer]"]
  C1 = Ceramic Capacitor [capacitance=10nF voltage=35V package="1206 [SMD, multilayer]"]
  C7 = Ceramic Capacitor [capacitance=10nF voltage=35V package="1206 [SMD, multilayer]"]
  C6 = Ceramic Capacitor [capacitance=10nF voltage=35V package="1206 [SMD, multilayer]"]
  C8 = Ceramic Capacitor [capacitance=10nF voltage=35V package="1206 [SMD, multilayer]"]
  R1 = Resistor [tolerance=±5% resistance=10k power=0.25 package="1206 [SMD]"]
  R3 = Resistor [tolerance=±5% resistance=10k power=0.25 package="1206 [SMD]"]
  R2 = Resistor [tolerance=±5% resistance=10k power=0.25 package="1206 [SMD]"]
  J1 = female pin header, 10 pins [form="♀ (female)"]
  MX1 = Cherry MX Keyswitch Simple

nets:
  N1: RE1.EncoderPinA, C7.0, R2.Pin_1, J1.pin8
  N2: RE1.EncoderPinC, RE1.SwitchrPinD, V1.V-, MX2.pin_1, MX3.pin_1, MX5.pin_1, MX4.pin_1, C11.0, C9.0, C10.0, C12.0, C1.0, C7.1, C6.1, C8.1, J1.pin7, MX1.pin_1
  N3: RE1.EncoderPinB, C6.0, R3.Pin_1, J1.pin9
  N4: RE1.SwitchPinE, C8.0, R1.Pin_0, J1.pin10
  N5: V1.V+, R1.Pin_1, R3.Pin_0, R2.Pin_0, J1.pin6
  N6: MX2.pin_2, C12.1, J1.pin2
  N7: MX3.pin_2, C11.1, J1.pin3
  N8: MX5.pin_2, C9.1, J1.pin5
  N9: MX4.pin_2, C10.1, J1.pin4
  N10: C1.1, J1.pin1, MX1.pin_2

notes:
  InputModule v1
  Esw
  S2
  Neg
  OutA
  S3
  S5
  3.3V
  S1
  S4
  OutB

custom parts:
  Rotary Encoder: Rotary Encoder from ALPSec11e with switch. This version has an alternate (which has been used in boards) pcb footprint from @opera_night in the forums. It is probably the best one to start from to see if you part matches.
  Cherry MX Keyswitch Simple: Cherry MX Keyswitch button for keyboards
